# Fritzing sketch led-test-bench (saved by Fritzing 0.9.3b)
breadboards: 1

parts:
  RE1 = Rotary Encoder [package=THT]
  RE2 = Rotary Encoder [package=THT]
  S1 = Pushbutton [package="[THT]"]
  J1 = Screw terminal - 2 pins [package=THT]  # not connected
  J2 = Screw terminal - 2 pins [package=THT]
  J3 = Screw terminal - 2 pins [package=THT]  # not connected
  Part1 = Arduino Uno (Rev3)
  J4 = Power Jack [package=power_jack_combo]

nets:
  N1: RE1.EncoderPinB, Part1.D9_PWM
  N2: RE2.EncoderPinB, Part1.D8
  N3: S1.Pin_1, S1.Pin_2, Part1.D10_PWM/SS, Part1.VIN
  N4: S1.Pin_3, S1.Pin_4, Part1.GND
  N5: J2.pin1, J4.GNDBREAK
  N6: J2.pin2, J4.GND
